// Logisim project lab7(group 2).circ as structural Verilog: 12 circuits, main circuit main
module main (
  input  C_in,
  input  [3:0] in_2,
  input  [3:0] in_3,
  input  [3:0] in_4,
  input  [15:0] Write_Data,
  input  Write_control,
  input  [1:0] select,
  output [15:0] Sum,
  output zero_flag,
  output overflow,
  output C_out
);

  wire clock_1_out;
  wire [15:0] n16_bit_register_file_1_read_data_1, n16_bit_register_file_1_read_data_2;

  _16_Bit_Register_File u_16_bit_register_file_1 (
    .Write_Data(Write_Data), .Read_Data_1(n16_bit_register_file_1_read_data_1),
    .Read_register_number_1(in_2), .Read_Data_2(n16_bit_register_file_1_read_data_2),
    .Read_register_number_2(in_3), .CLK(clock_1_out), .Write_Register(in_4), .write_control(Write_control));
  Clock clock_1 (.out(clock_1_out));
  _16_bit_ALU u_16_bit_alu_1 (
    .c_in(C_in), .A(n16_bit_register_file_1_read_data_1), .B(n16_bit_register_file_1_read_data_2),
    .select(select), .SUM(Sum), .zero_flag(zero_flag), .Overflow_check(overflow), .C_out(C_out));
endmodule

module _16_Bit_Register_File (
  input  [15:0] Write_Data,
  input  [3:0] Read_register_number_1,
  input  [3:0] Write_Register,
  input  [3:0] Read_register_number_2,
  input  write_control,
  input  CLK,
  output [15:0] Read_Data_1,
  output [15:0] Read_Data_2
);

  wire and_1_out, and_2_out, and_3_out, and_4_out, and_5_out, and_6_out, and_7_out, and_8_out, and_9_out,
       and_10_out, and_11_out, and_12_out, and_13_out, and_14_out, and_15_out, and_16_out, decoder_1_out0,
       decoder_1_out1, decoder_1_out2, decoder_1_out3, decoder_1_out4, decoder_1_out5, decoder_1_out6,
       decoder_1_out7, decoder_1_out8, decoder_1_out9, decoder_1_out10, decoder_1_out11, decoder_1_out12,
       decoder_1_out13, decoder_1_out14, decoder_1_out15;
  wire [15:0] _0_q, _1_q, _2_q, _3_q, _4_q, _5_q, _6_q, _7_q, _8_q, _9_q, _10_q, _11_q, _12_q, _13_q, _14_q,
       _15_q;

  Decoder #(.select(4), .enable("false")) decoder_1 (
    .out0(decoder_1_out0), .out1(decoder_1_out1), .out2(decoder_1_out2), .out3(decoder_1_out3),
    .out4(decoder_1_out4), .out5(decoder_1_out5), .out6(decoder_1_out6), .out7(decoder_1_out7),
    .out8(decoder_1_out8), .out9(decoder_1_out9), .out10(decoder_1_out10), .out11(decoder_1_out11),
    .out12(decoder_1_out12), .out13(decoder_1_out13), .out14(decoder_1_out14), .out15(decoder_1_out15),
    .sel(Write_Register));
  and and_1 (and_1_out, decoder_1_out0, write_control);
  and and_2 (and_2_out, decoder_1_out1, write_control);
  and and_3 (and_3_out, decoder_1_out2, write_control);
  and and_4 (and_4_out, decoder_1_out3, write_control);
  and and_5 (and_5_out, decoder_1_out4, write_control);
  and and_6 (and_6_out, decoder_1_out5, write_control);
  and and_7 (and_7_out, decoder_1_out6, write_control);
  and and_8 (and_8_out, decoder_1_out7, write_control);
  and and_9 (and_9_out, decoder_1_out8, write_control);
  and and_10 (and_10_out, decoder_1_out9, write_control);
  and and_11 (and_11_out, decoder_1_out10, write_control);
  and and_12 (and_12_out, decoder_1_out11, write_control);
  and and_13 (and_13_out, decoder_1_out12, write_control);
  and and_14 (and_14_out, decoder_1_out13, write_control);
  and and_15 (and_15_out, decoder_1_out14, write_control);
  and and_16 (and_16_out, decoder_1_out15, write_control);
  Register #(.width(16)) _0 (.D(Write_Data), .en(and_1_out), .Q(_0_q), .clk(CLK));  // open: clr
  Register #(.width(16)) _1 (.D(Write_Data), .en(and_2_out), .Q(_1_q), .clk(CLK));  // open: clr
  Register #(.width(16)) _2 (.D(Write_Data), .en(and_3_out), .Q(_2_q), .clk(CLK));  // open: clr
  Register #(.width(16)) _3 (.D(Write_Data), .en(and_4_out), .Q(_3_q), .clk(CLK));  // open: clr
  Register #(.width(16)) _4 (.D(Write_Data), .en(and_5_out), .Q(_4_q), .clk(CLK));  // open: clr
  Register #(.width(16)) _5 (.D(Write_Data), .en(and_6_out), .Q(_5_q), .clk(CLK));  // open: clr
  Register #(.width(16)) _6 (.D(Write_Data), .en(and_7_out), .Q(_6_q), .clk(CLK));  // open: clr
  Register #(.width(16)) _7 (.D(Write_Data), .en(and_8_out), .Q(_7_q), .clk(CLK));  // open: clr
  Register #(.width(16)) _8 (.D(Write_Data), .en(and_9_out), .Q(_8_q), .clk(CLK));  // open: clr
  Register #(.width(16)) _9 (.D(Write_Data), .en(and_10_out), .Q(_9_q), .clk(CLK));  // open: clr
  Register #(.width(16)) _10 (.D(Write_Data), .en(and_11_out), .Q(_10_q), .clk(CLK));  // open: clr
  Register #(.width(16)) _11 (.D(Write_Data), .en(and_12_out), .Q(_11_q), .clk(CLK));  // open: clr
  Register #(.width(16)) _12 (.D(Write_Data), .en(and_13_out), .Q(_12_q), .clk(CLK));  // open: clr
  Register #(.width(16)) _13 (.D(Write_Data), .en(and_14_out), .Q(_13_q), .clk(CLK));  // open: clr
  Register #(.width(16)) _14 (.D(Write_Data), .en(and_15_out), .Q(_14_q), .clk(CLK));  // open: clr
  Register #(.width(16)) _15 (.D(Write_Data), .en(and_16_out), .Q(_15_q), .clk(CLK));  // open: clr
  Multiplexer #(.select(4), .width(16), .enable("false")) multiplexer_1 (
    .in0(_0_q), .in1(_1_q), .in2(_2_q), .in3(_3_q), .in4(_4_q), .in5(_5_q), .in6(_6_q), .in7(_7_q),
    .in8(_8_q), .in9(_9_q), .in10(_10_q), .in11(_11_q), .in12(_12_q), .in13(_13_q), .in14(_14_q),
    .in15(_15_q), .out(Read_Data_1), .sel(Read_register_number_1));
  Multiplexer #(.select(4), .width(16), .enable("false")) multiplexer_2 (
    .in0(_0_q), .in1(_1_q), .in2(_2_q), .in3(_3_q), .in4(_4_q), .in5(_5_q), .in6(_6_q), .in7(_7_q),
    .in8(_8_q), .in9(_9_q), .in10(_10_q), .in11(_11_q), .in12(_12_q), .in13(_13_q), .in14(_14_q),
    .in15(_15_q), .out(Read_Data_2), .sel(Read_register_number_2));
endmodule

module _1_bit_ALU (
  input  c_in,
  input  A,
  input  B,
  input  [1:0] select,
  output Sum,
  output C_out
);

  wire and_1_out, and_2_out, multiplexer_1_out, not_1_out, or_1_out;

  not not_1 (not_1_out, B);
  and and_1 (and_1_out, A, B);
  or or_1 (or_1_out, A, B);
  Multiplexer #(.enable("false")) multiplexer_1 (.in0(B), .in1(not_1_out), .out(multiplexer_1_out), .sel(and_2_out));
  Adder #(.width(1)) adder_1 (.a(A), .b(multiplexer_1_out), .cin(c_in), .cout(C_out));  // open: out
  and and_2 (and_2_out, select[0], c_in, select[1]);
  Multiplexer #(.select(2), .enable("false")) multiplexer_2 (
    .in0(and_1_out), .in1(or_1_out), .out(Sum), .sel(select));  // open: in2, in3
endmodule

module _16_bit_ALU (
  input  c_in,
  input  [15:0] A,
  input  [15:0] B,
  input  [1:0] select,
  output [15:0] SUM,
  output zero_flag,
  output Overflow_check,
  output C_out
);

  wire n1_bit_alu_1_c_out, n1_bit_alu_2_c_out, n1_bit_alu_3_c_out, n1_bit_alu_4_c_out, n1_bit_alu_5_c_out,
       n1_bit_alu_6_c_out, n1_bit_alu_7_c_out, n1_bit_alu_8_c_out, n1_bit_alu_9_c_out, n1_bit_alu_10_c_out,
       n1_bit_alu_11_c_out, n1_bit_alu_12_c_out, n1_bit_alu_13_c_out, n1_bit_alu_14_c_out,
       n1_bit_alu_15_c_out;

  _1_bit_ALU u_1_bit_alu_1 (.c_in(c_in), .A(A[0]), .B(B[0]), .select(select), .Sum(SUM[0]), .C_out(n1_bit_alu_1_c_out));
  _1_bit_ALU u_1_bit_alu_2 (
    .c_in(n1_bit_alu_1_c_out), .A(A[1]), .B(B[1]), .select(select), .Sum(SUM[1]), .C_out(n1_bit_alu_2_c_out));
  _1_bit_ALU u_1_bit_alu_3 (
    .c_in(n1_bit_alu_2_c_out), .A(A[2]), .B(B[2]), .select(select), .Sum(SUM[2]), .C_out(n1_bit_alu_3_c_out));
  _1_bit_ALU u_1_bit_alu_4 (
    .c_in(n1_bit_alu_3_c_out), .A(A[3]), .B(B[3]), .select(select), .Sum(SUM[3]), .C_out(n1_bit_alu_4_c_out));
  _1_bit_ALU u_1_bit_alu_5 (
    .c_in(n1_bit_alu_4_c_out), .A(A[4]), .B(B[4]), .select(select), .Sum(SUM[4]), .C_out(n1_bit_alu_5_c_out));
  _1_bit_ALU u_1_bit_alu_6 (
    .c_in(n1_bit_alu_5_c_out), .A(A[5]), .B(B[5]), .select(select), .Sum(SUM[5]), .C_out(n1_bit_alu_6_c_out));
  _1_bit_ALU u_1_bit_alu_7 (
    .c_in(n1_bit_alu_6_c_out), .A(A[6]), .B(A[7]), .select(select), .Sum(SUM[6]), .C_out(n1_bit_alu_7_c_out));
  _1_bit_ALU u_1_bit_alu_8 (
    .c_in(n1_bit_alu_7_c_out), .A(A[7]), .B(B[7]), .select(select), .Sum(SUM[7]), .C_out(n1_bit_alu_8_c_out));
  _1_bit_ALU u_1_bit_alu_9 (
    .c_in(n1_bit_alu_8_c_out), .A(A[8]), .B(B[8]), .select(select), .Sum(SUM[8]), .C_out(n1_bit_alu_9_c_out));
  _1_bit_ALU u_1_bit_alu_10 (
    .c_in(n1_bit_alu_9_c_out), .A(A[9]), .B(B[9]), .select(select), .Sum(SUM[9]), .C_out(n1_bit_alu_10_c_out));
  _1_bit_ALU u_1_bit_alu_11 (
    .c_in(n1_bit_alu_10_c_out), .A(A[10]), .B(B[10]), .select(select), .Sum(SUM[10]),
    .C_out(n1_bit_alu_11_c_out));
  _1_bit_ALU u_1_bit_alu_12 (
    .c_in(n1_bit_alu_11_c_out), .A(A[11]), .B(B[11]), .select(select), .Sum(SUM[11]),
    .C_out(n1_bit_alu_12_c_out));
  _1_bit_ALU u_1_bit_alu_13 (
    .c_in(n1_bit_alu_12_c_out), .A(A[12]), .B(B[12]), .select(select), .Sum(SUM[12]),
    .C_out(n1_bit_alu_13_c_out));
  _1_bit_ALU u_1_bit_alu_14 (
    .c_in(n1_bit_alu_13_c_out), .A(A[13]), .B(B[13]), .select(select), .Sum(SUM[13]),
    .C_out(n1_bit_alu_14_c_out));
  _1_bit_ALU u_1_bit_alu_15 (
    .c_in(n1_bit_alu_14_c_out), .A(A[14]), .B(B[14]), .select(select), .Sum(SUM[14]),
    .C_out(n1_bit_alu_15_c_out));
  _1_bit_ALU u_1_bit_alu_16 (
    .c_in(n1_bit_alu_15_c_out), .A(A[15]), .B(B[15]), .select(select), .Sum(SUM[15]), .C_out(C_out));
  xor xor_1 (Overflow_check, n1_bit_alu_15_c_out, C_out);
  nor nor_1 (zero_flag, SUM[0], SUM[1], SUM[2], SUM[3], SUM[4], SUM[5], SUM[6], SUM[7], SUM[8], SUM[9], SUM[10], SUM[11], SUM[12], SUM[13], SUM[14], SUM[15]);

  assign B[6] = A[7];
endmodule

module R_type (
  input  Cin
);

  wire clock_1_out, n16_bit_alu_1_c_out, n16_bit_alu_1_overflow_check, n16_bit_alu_1_zero_flag, undriven;
  wire [1:0] bit_extender_1_out;
  wire [15:0] adder_1_out, n16_bit_alu_1_sum, n16_bit_register_file_1_read_data_1,
       n16_bit_register_file_1_read_data_2, register_1_q, rom_1_data;

  Clock clock_1 (.out(clock_1_out));
  Register #(.width(16)) register_1 (.D(adder_1_out), .Q(register_1_q), .clk(clock_1_out));  // open: en, clr
  Adder #(.width(16)) adder_1 (.a(16'h1), .b(register_1_q), .out(adder_1_out));  // open: cin, cout
  ROM #(.addrWidth(16), .dataWidth(16)) rom_1 (.addr(register_1_q), .data(rom_1_data));  // open: sel
  _16_Bit_Register_File u_16_bit_register_file_1 (
    .Write_Data(n16_bit_alu_1_sum), .Read_Data_1(n16_bit_register_file_1_read_data_1),
    .Read_register_number_1(rom_1_data[7:4]), .Read_Data_2(n16_bit_register_file_1_read_data_2),
    .Read_register_number_2(rom_1_data[3:0]), .CLK(clock_1_out), .Write_Register(rom_1_data[11:8]),
    .write_control(undriven));
  Bit_Extender #(.in_width(4), .out_width(2)) bit_extender_1 (.in(rom_1_data[15:12]), .out(bit_extender_1_out));
  _16_bit_ALU u_16_bit_alu_1 (
    .c_in(Cin), .A(n16_bit_register_file_1_read_data_1), .B(n16_bit_register_file_1_read_data_2),
    .select(bit_extender_1_out), .SUM(n16_bit_alu_1_sum), .zero_flag(n16_bit_alu_1_zero_flag),
    .Overflow_check(n16_bit_alu_1_overflow_check), .C_out(n16_bit_alu_1_c_out));
endmodule

module I_type (
  input  Cin,
  input  Write_Control,
  output overflow,
  output zero_flag
);

  wire clock_1_out, n16_bit_alu_1_c_out, undriven, undriven_2;
  wire [1:0] bit_extender_2_out;
  wire [15:0] adder_1_out, bit_extender_1_out, n16_bit_alu_1_sum, n16_bit_register_file_1_read_data_1,
       n16_bit_register_file_1_read_data_2, ram_1_data, register_1_q, rom_1_data;

  Clock clock_1 (.out(clock_1_out));
  Register #(.width(16)) register_1 (.D(adder_1_out), .Q(register_1_q), .clk(clock_1_out));  // open: en, clr
  Adder #(.width(16)) adder_1 (.a(16'h1), .b(register_1_q), .out(adder_1_out));  // open: cin, cout
  ROM #(.addrWidth(16), .dataWidth(16)) rom_1 (.addr(register_1_q), .data(rom_1_data));  // open: sel
  assign bit_extender_1_out = {{12{1'b0}}, rom_1_data[3:0]};  // Bit_Extender bit_extender_1
  _16_Bit_Register_File u_16_bit_register_file_1 (
    .Write_Data(ram_1_data), .Read_Data_1(n16_bit_register_file_1_read_data_1),
    .Read_register_number_1(rom_1_data[7:4]), .Read_Data_2(n16_bit_register_file_1_read_data_2),
    .Read_register_number_2(rom_1_data[7:4]), .CLK(clock_1_out), .Write_Register(rom_1_data[11:8]),
    .write_control(Write_Control));
  Bit_Extender #(.in_width(4), .out_width(2)) bit_extender_2 (.in(rom_1_data[15:12]), .out(bit_extender_2_out));
  _16_bit_ALU u_16_bit_alu_1 (
    .c_in(Cin), .A(n16_bit_register_file_1_read_data_1), .B(bit_extender_1_out), .select(bit_extender_2_out),
    .SUM(n16_bit_alu_1_sum), .zero_flag(zero_flag), .Overflow_check(overflow), .C_out(n16_bit_alu_1_c_out));
  RAM #(.addrWidth(16), .dataWidth(16), .bus("separate")) ram_1 (
    .addr(n16_bit_alu_1_sum), .din(n16_bit_register_file_1_read_data_2), .data(ram_1_data), .str(undriven),
    .clk(clock_1_out), .ld(undriven_2));  // open: sel, clr
endmodule

module Combiined_datapath (
  input  Cin,
  input  Write_Control,
  input  select,
  output overflow,
  output zero_flag
);

  wire clock_1_out, n16_bit_alu_1_c_out, undriven, undriven_2;
  wire [1:0] bit_extender_2_out;
  wire [3:0] multiplexer_1_out;
  wire [15:0] adder_1_out, bit_extender_1_out, multiplexer_2_out, multiplexer_3_out, n16_bit_alu_1_sum,
       n16_bit_register_file_1_read_data_1, n16_bit_register_file_1_read_data_2, ram_1_data, register_1_q,
       rom_1_data;

  Clock clock_1 (.out(clock_1_out));
  Register #(.width(16)) register_1 (.D(adder_1_out), .Q(register_1_q), .clk(clock_1_out));  // open: en, clr
  Adder #(.width(16)) adder_1 (.a(16'h1), .b(register_1_q), .out(adder_1_out));  // open: cin, cout
  ROM #(.addrWidth(16), .dataWidth(16)) rom_1 (.addr(register_1_q), .data(rom_1_data));  // open: sel
  Multiplexer #(.width(4), .enable("false")) multiplexer_1 (
    .in0(rom_1_data[3:0]), .in1(rom_1_data[7:4]), .out(multiplexer_1_out), .sel(select));
  assign bit_extender_1_out = {{12{1'b0}}, rom_1_data[3:0]};  // Bit_Extender bit_extender_1
  _16_Bit_Register_File u_16_bit_register_file_1 (
    .Write_Data(multiplexer_3_out), .Read_Data_1(n16_bit_register_file_1_read_data_1),
    .Read_register_number_1(rom_1_data[7:4]), .Read_Data_2(n16_bit_register_file_1_read_data_2),
    .Read_register_number_2(multiplexer_1_out), .CLK(clock_1_out), .Write_Register(rom_1_data[11:8]),
    .write_control(Write_Control));
  _16_bit_ALU u_16_bit_alu_1 (
    .c_in(Cin), .A(n16_bit_register_file_1_read_data_1), .B(multiplexer_2_out), .select(bit_extender_2_out),
    .SUM(n16_bit_alu_1_sum), .zero_flag(zero_flag), .Overflow_check(overflow), .C_out(n16_bit_alu_1_c_out));
  Bit_Extender #(.in_width(4), .out_width(2)) bit_extender_2 (.in(rom_1_data[15:12]), .out(bit_extender_2_out));
  Multiplexer #(.width(16), .enable("false")) multiplexer_2 (
    .in0(n16_bit_register_file_1_read_data_2), .in1(bit_extender_1_out), .out(multiplexer_2_out), .sel(select));
  RAM #(.addrWidth(16), .dataWidth(16), .bus("separate")) ram_1 (
    .addr(n16_bit_alu_1_sum), .din(n16_bit_register_file_1_read_data_2), .data(ram_1_data), .str(undriven),
    .clk(clock_1_out), .ld(undriven_2));  // open: sel, clr
  Multiplexer #(.width(16), .enable("false")) multiplexer_3 (
    .in0(n16_bit_alu_1_sum), .in1(ram_1_data), .out(multiplexer_3_out), .sel(select));
endmodule

module IF_ID (
  input  [15:0] in_1,
  input  clock,
  output [15:0] out_3
);

  Register #(.width(16)) register_1 (.D(in_1), .Q(out_3), .clk(clock));  // open: en, clr
endmodule

module pipeline_combined (
  input  Cin,
  input  Write_Control,
  input  select
);

  wire clock_1_out, n16_bit_alu_1_c_out, undriven, undriven_2;
  wire [1:0] bit_extender_2_out, id_ex_1_out_8;
  wire [3:0] multiplexer_1_out;
  wire [15:0] adder_1_out, bit_extender_1_out, ex_mem_1_out_4, ex_mem_1_out_5, id_ex_1_out_6, id_ex_1_out_7,
       id_ex_1_out_9, if_id_1_out_3, mem_wb_1_out_4, mem_wb_1_out_5, multiplexer_2_out, multiplexer_3_out,
       n16_bit_alu_1_sum, n16_bit_register_file_1_read_data_1, n16_bit_register_file_1_read_data_2,
       ram_1_data, register_1_q, rom_1_data;

  Clock clock_1 (.out(clock_1_out));
  Register #(.width(16)) register_1 (.D(adder_1_out), .Q(register_1_q), .clk(clock_1_out));  // open: en, clr
  Adder #(.width(16)) adder_1 (.a(16'h1), .b(register_1_q), .out(adder_1_out));  // open: cin, cout
  ROM #(.addrWidth(16), .dataWidth(16)) rom_1 (.addr(register_1_q), .data(rom_1_data));  // open: sel
  IF_ID if_id_1 (.in_1(rom_1_data), .out_3(if_id_1_out_3), .clock(clock_1_out));
  Multiplexer #(.width(4), .enable("false")) multiplexer_1 (
    .in0(if_id_1_out_3[3:0]), .in1(if_id_1_out_3[7:4]), .out(multiplexer_1_out), .sel(select));
  assign bit_extender_1_out = {{12{1'b0}}, if_id_1_out_3[3:0]};  // Bit_Extender bit_extender_1
  _16_Bit_Register_File u_16_bit_register_file_1 (
    .Write_Data(multiplexer_3_out), .Read_Data_1(n16_bit_register_file_1_read_data_1),
    .Read_register_number_1(if_id_1_out_3[7:4]), .Read_Data_2(n16_bit_register_file_1_read_data_2),
    .Read_register_number_2(multiplexer_1_out), .CLK(clock_1_out), .Write_Register(if_id_1_out_3[11:8]),
    .write_control(Write_Control));
  Bit_Extender #(.in_width(4), .out_width(2)) bit_extender_2 (.in(if_id_1_out_3[15:12]), .out(bit_extender_2_out));
  Multiplexer #(.width(16), .enable("false")) multiplexer_2 (
    .in0(n16_bit_register_file_1_read_data_2), .in1(bit_extender_1_out), .out(multiplexer_2_out), .sel(select));
  ID_EX id_ex_1 (
    .in_1(n16_bit_register_file_1_read_data_1), .in_2(multiplexer_2_out), .in_3(bit_extender_2_out),
    .in_4(n16_bit_register_file_1_read_data_2), .clock(clock_1_out), .out_6(id_ex_1_out_6),
    .out_7(id_ex_1_out_7), .out_8(id_ex_1_out_8), .out_9(id_ex_1_out_9));
  _16_bit_ALU u_16_bit_alu_1 (
    .c_in(Cin), .A(id_ex_1_out_6), .B(id_ex_1_out_7), .select(id_ex_1_out_8), .SUM(n16_bit_alu_1_sum),
    .C_out(n16_bit_alu_1_c_out));  // open: zero_flag, Overflow_check
  EX_MEM ex_mem_1 (
    .in_1(n16_bit_alu_1_sum), .in_2(id_ex_1_out_9), .clock(clock_1_out), .out_4(ex_mem_1_out_4),
    .out_5(ex_mem_1_out_5));
  RAM #(.addrWidth(16), .dataWidth(16), .bus("separate")) ram_1 (
    .addr(ex_mem_1_out_4), .din(ex_mem_1_out_5), .data(ram_1_data), .str(undriven), .clk(clock_1_out),
    .ld(undriven_2));  // open: sel, clr
  MEM_WB mem_wb_1 (
    .in_1(ex_mem_1_out_4), .in_2(ram_1_data), .clock(clock_1_out), .out_4(mem_wb_1_out_4),
    .out_5(mem_wb_1_out_5));
  Multiplexer #(.width(16), .enable("false")) multiplexer_3 (
    .in0(mem_wb_1_out_4), .in1(mem_wb_1_out_5), .out(multiplexer_3_out), .sel(select));
endmodule

module ID_EX (
  input  [15:0] in_1,
  input  [15:0] in_2,
  input  [1:0] in_3,
  input  [15:0] in_4,
  input  clock,
  output [15:0] out_6,
  output [15:0] out_7,
  output [1:0] out_8,
  output [15:0] out_9
);

  Register #(.width(16)) register_1 (.D(in_1), .Q(out_6), .clk(clock));  // open: en, clr
  Register #(.width(16)) register_2 (.D(in_2), .Q(out_7), .clk(clock));  // open: en, clr
  Register #(.width(2)) register_3 (.D(in_3), .Q(out_8), .clk(clock));  // open: en, clr
  Register #(.width(16)) register_4 (.D(in_4), .Q(out_9), .clk(clock));  // open: en, clr
endmodule

module EX_MEM (
  input  [15:0] in_1,
  input  [15:0] in_2,
  input  clock,
  output [15:0] out_4,
  output [15:0] out_5
);

  Register #(.width(16)) register_1 (.D(in_1), .Q(out_4), .clk(clock));  // open: en, clr
  Register #(.width(16)) register_2 (.D(in_2), .Q(out_5), .clk(clock));  // open: en, clr
endmodule

module MEM_WB (
  input  [15:0] in_1,
  input  [15:0] in_2,
  input  clock,
  output [15:0] out_4,
  output [15:0] out_5
);

  Register #(.width(16)) register_1 (.D(in_1), .Q(out_4), .clk(clock));  // open: en, clr
  Register #(.width(16)) register_2 (.D(in_2), .Q(out_5), .clk(clock));  // open: en, clr
endmodule
